// Logisim project ax8.circ as structural Verilog
module register_file (
  input  CLK,
  input  RST,
  input  [2:0] RDA_SEL,
  input  [2:0] RDB_SEL,
  input  WE,
  input  [2:0] WR_SEL,
  input  [1:0] WR_MODE,
  input  [15:0] WR_DATA,
  output [7:0] RDA_DATA,
  output [7:0] RDB_DATA,
  output [15:0] Z_DATA,
  output [15:0] SP_DATA
);

  wire adder_subtractor_1_cout, adder_subtractor_1_vout, adder_subtractor_2_cout, adder_subtractor_2_vout,
       DEC, demultiplexer_1_out1, INC, INC_CIN, IS_INC_DEC, or_3_out, or_4_out, or_5_out, or_6_out, WE_REG_A,
       WE_REG_B, WE_REG_C, WE_REG_D, WE_REG_H, WE_REG_L, WE_REG_SP, WE_REG_X, WE_REG_Y, WE_REG_Z, WR8, WR16;
  wire [7:0] adder_subtractor_2_y, HI_R16, LO_R16, multiplexer_3_out, multiplexer_4_out, multiplexer_5_out,
       multiplexer_6_out, REG_A_Q, REG_B_Q, REG_C_Q, REG_D_Q;

  Demultiplexer #(.select(2)) demultiplexer_1 (
    .out0(WR8), .out1(demultiplexer_1_out1), .out2(INC), .out3(DEC), .in(WE), .sel(WR_MODE));
  Demultiplexer #(.select(3)) demultiplexer_2 (
    .out0(WE_REG_A), .out1(WE_REG_B), .out2(WE_REG_C), .out3(WE_REG_D), .out4(WE_REG_X), .out5(WE_REG_Y),
    .out6(WE_REG_H), .out7(WE_REG_L), .in(WR8), .sel(WR_SEL));
  Demultiplexer demultiplexer_3 (.out0(WE_REG_Z), .out1(WE_REG_SP), .in(WR16), .sel(WR_SEL[0]));
  and and_1 (INC_CIN, INC, ~DEC);  // AND_Gate
  or or_1 (IS_INC_DEC, INC, DEC);
  or or_2 (WR16, demultiplexer_1_out1, INC, DEC);
  Multiplexer #(.select(3), .width(8)) multiplexer_1 (
    .in0(REG_A_Q), .in1(REG_B_Q), .in2(REG_C_Q), .in3(REG_D_Q), .in4(Z_DATA[7:0]), .in5(Z_DATA[15:8]),
    .in6(SP_DATA[15:8]), .in7(SP_DATA[7:0]), .out(RDA_DATA), .sel(RDA_SEL));
  Register reg_a (.D(WR_DATA[7:0]), .en(WE_REG_A), .clk(CLK), .Q(REG_A_Q), .clr(RST));
  Register reg_b (.D(WR_DATA[7:0]), .en(WE_REG_B), .clk(CLK), .Q(REG_B_Q), .clr(RST));
  Register reg_c (.D(WR_DATA[7:0]), .en(WE_REG_C), .clk(CLK), .Q(REG_C_Q), .clr(RST));
  Register reg_d (.D(WR_DATA[7:0]), .en(WE_REG_D), .clk(CLK), .Q(REG_D_Q), .clr(RST));
  Multiplexer #(.select(3), .width(8)) multiplexer_2 (
    .in0(REG_A_Q), .in1(REG_B_Q), .in2(REG_C_Q), .in3(REG_D_Q), .in4(Z_DATA[7:0]), .in5(Z_DATA[15:8]),
    .in6(SP_DATA[15:8]), .in7(SP_DATA[7:0]), .out(RDB_DATA), .sel(RDB_SEL));
  or or_3 (or_3_out, WE_REG_X, WE_REG_Z);
  or or_4 (or_4_out, WE_REG_H, WE_REG_SP);
  Multiplexer #(.width(8)) multiplexer_3 (
    .in0(Z_DATA[7:0]), .in1(SP_DATA[7:0]), .out(multiplexer_3_out), .sel(WR_SEL[0]));
  Multiplexer #(.width(8)) multiplexer_4 (
    .in0(Z_DATA[15:8]), .in1(SP_DATA[15:8]), .out(multiplexer_4_out), .sel(WR_SEL[0]));
  Register reg_x (.D(LO_R16), .en(or_3_out), .clk(CLK), .Q(Z_DATA[7:0]), .clr(RST));
  Register reg_l (.D(LO_R16), .en(or_4_out), .clk(CLK), .Q(SP_DATA[7:0]), .clr(RST));
  Multiplexer #(.width(8)) multiplexer_5 (
    .in0(WR_DATA[7:0]), .in1(multiplexer_3_out), .out(multiplexer_5_out), .sel(IS_INC_DEC));
  Multiplexer #(.width(8)) multiplexer_6 (
    .in0(WR_DATA[15:8]), .in1(multiplexer_4_out), .out(multiplexer_6_out), .sel(IS_INC_DEC));
  or or_5 (or_5_out, WE_REG_Y, WE_REG_Z);
  or or_6 (or_6_out, WE_REG_L, WE_REG_SP);
  Register reg_y (.D(HI_R16), .en(or_5_out), .clk(CLK), .Q(Z_DATA[15:8]), .clr(RST));
  Register reg_h (.D(HI_R16), .en(or_6_out), .clk(CLK), .Q(SP_DATA[15:8]), .clr(RST));
  adder_subtractor adder_subtractor_1 (
    .A(multiplexer_5_out), .B({8{1'b0}}), .CIN(INC_CIN), .MODE(DEC), .Y(LO_R16),
    .COUT(adder_subtractor_1_cout), .VOUT(adder_subtractor_1_vout));
  // NoConnect on adder_subtractor_1_vout
  adder_subtractor adder_subtractor_2 (
    .A(multiplexer_6_out), .B({8{1'b0}}), .CIN(adder_subtractor_1_cout), .MODE(DEC),
    .Y(adder_subtractor_2_y), .COUT(adder_subtractor_2_cout), .VOUT(adder_subtractor_2_vout));
  // NoConnect on adder_subtractor_2_cout
  // NoConnect on adder_subtractor_2_vout
  Multiplexer #(.width(8)) multiplexer_7 (.in0(LO_R16), .in1(adder_subtractor_2_y), .out(HI_R16), .sel(WR16));

  // Other names for the same wires on the sheet: REG_L_Q[7:0] = SP_DATA[7:0]; REG_H_Q[7:0] = SP_DATA[15:8];
  //   WR_DATA_L[7:0] = WR_DATA[7:0]; WR_DATA_H[7:0] = WR_DATA[15:8]; REG_X_Q[7:0] = Z_DATA[7:0];
  //   REG_Y_Q[7:0] = Z_DATA[15:8]
endmodule

module adder_subtractor (
  input  [7:0] A,
  input  [7:0] B,
  input  CIN,
  input  MODE,
  output [7:0] Y,
  output COUT,
  output VOUT
);

  wire B0, B1, B2, B3, B4, B5, B6, B7, full_adder_1_cout, full_adder_2_cout, full_adder_3_cout,
       full_adder_4_cout, full_adder_5_cout, full_adder_6_cout, full_adder_7_cout;

  assign {B7, B6, B5, B4, B3, B2, B1, B0} = B ^ {8{MODE}};  // XOR_Gate xor_1, 8 bits wide
  full_adder full_adder_1 (.A(A[0]), .B(B0), .CIN(CIN), .Y(Y[0]), .COUT(full_adder_1_cout));
  full_adder full_adder_2 (.A(A[1]), .B(B1), .CIN(full_adder_1_cout), .Y(Y[1]), .COUT(full_adder_2_cout));
  full_adder full_adder_3 (.A(A[2]), .B(B2), .CIN(full_adder_2_cout), .Y(Y[2]), .COUT(full_adder_3_cout));
  full_adder full_adder_4 (.A(A[3]), .B(B3), .CIN(full_adder_3_cout), .Y(Y[3]), .COUT(full_adder_4_cout));
  full_adder full_adder_5 (.A(A[4]), .B(B4), .CIN(full_adder_4_cout), .Y(Y[4]), .COUT(full_adder_5_cout));
  full_adder full_adder_6 (.A(A[5]), .B(B5), .CIN(full_adder_5_cout), .Y(Y[5]), .COUT(full_adder_6_cout));
  full_adder full_adder_7 (.A(A[6]), .B(B6), .CIN(full_adder_6_cout), .Y(Y[6]), .COUT(full_adder_7_cout));
  full_adder full_adder_8 (.A(A[7]), .B(B7), .CIN(full_adder_7_cout), .Y(Y[7]), .COUT(COUT));
  xor xor_2 (VOUT, full_adder_7_cout, COUT);
endmodule

module full_adder (
  input  A,
  input  B,
  input  CIN,
  output Y,
  output COUT
);

  wire and_1_out, and_2_out, xor_1_out;

  xor xor_1 (xor_1_out, A, B);
  and and_1 (and_1_out, xor_1_out, CIN);
  and and_2 (and_2_out, A, B);
  xor xor_2 (Y, xor_1_out, CIN);
  or or_1 (COUT, and_1_out, and_2_out);
endmodule
